// Logisim project psMCU.circ as structural Verilog: 13 circuits, main circuit main
module FullAdder (
  input  A,
  input  B,
  input  Cin,
  output Out,
  output Cout
);

  wire and_1_out, and_2_out, xor_1_out;

  xor xor_1 (xor_1_out, A, B);
  xor xor_2 (Out, xor_1_out, Cin);
  and and_1 (and_1_out, xor_1_out, Cin);
  and and_2 (and_2_out, B, A);
  or or_1 (Cout, and_1_out, and_2_out);
endmodule

module Complementer (
  input  [7:0] IN,
  output [7:0] OUT
);

  wire and_1_out, and_2_out, and_3_out, and_4_out, and_5_out, and_6_out, and_7_out;
  wire [7:0] not_1_out;

  and and_1 (and_1_out, and_2_out, not_1_out[6]);
  xor xor_1 (OUT[7], not_1_out[7], and_1_out);
  xor xor_2 (OUT[6], not_1_out[6], and_2_out);
  and and_2 (and_2_out, and_3_out, not_1_out[5]);
  xor xor_3 (OUT[5], not_1_out[5], and_3_out);
  assign not_1_out = ~IN;  // NOT_Gate not_1, 8 bits wide
  and and_3 (and_3_out, and_4_out, not_1_out[4]);
  xor xor_4 (OUT[4], not_1_out[4], and_4_out);
  and and_4 (and_4_out, and_5_out, not_1_out[3]);
  xor xor_5 (OUT[3], not_1_out[3], and_5_out);
  and and_5 (and_5_out, and_6_out, not_1_out[2]);
  and and_6 (and_6_out, and_7_out, not_1_out[1]);
  xor xor_6 (OUT[2], not_1_out[2], and_6_out);
  xor xor_7 (OUT[1], not_1_out[1], and_7_out);
  and and_7 (and_7_out, 1'b1, not_1_out[0]);
  xor xor_8 (OUT[0], not_1_out[0], 1'b1);

  // Notes on the sheet:
  //   LSB Could be just one not gate, if it reduces chip count
endmodule

module BarrelShifter (
  input  [7:0] Register_A,
  input  Shift_In,
  input  R,
  input  [2:0] Operand_B,
  output [7:0] OUT
);

  wire multiplexer_1_out, multiplexer_2_out, multiplexer_3_out, multiplexer_4_out, multiplexer_6_out,
       multiplexer_7_out, multiplexer_8_out, multiplexer_9_out, multiplexer_10_out, multiplexer_12_out,
       multiplexer_13_out, multiplexer_14_out, multiplexer_16_out, multiplexer_17_out, multiplexer_18_out,
       multiplexer_19_out, multiplexer_21_out, multiplexer_22_out, multiplexer_23_out, multiplexer_24_out,
       multiplexer_26_out, multiplexer_27_out, multiplexer_28_out, multiplexer_29_out, multiplexer_31_out,
       multiplexer_32_out, multiplexer_33_out, multiplexer_34_out, multiplexer_36_out, multiplexer_37_out,
       multiplexer_38_out, multiplexer_39_out;

  Multiplexer #(.enable("false")) multiplexer_1 (
    .in0(Register_A[7]), .in1(Register_A[0]), .out(multiplexer_1_out), .sel(R));
  Multiplexer #(.enable("false")) multiplexer_2 (
    .in0(multiplexer_1_out), .in1(multiplexer_6_out), .out(multiplexer_2_out), .sel(Operand_B[0]));
  Multiplexer #(.enable("false")) multiplexer_3 (
    .in0(multiplexer_2_out), .in1(multiplexer_12_out), .out(multiplexer_3_out), .sel(Operand_B[1]));
  Multiplexer #(.enable("false")) multiplexer_4 (
    .in0(multiplexer_3_out), .in1(multiplexer_23_out), .out(multiplexer_4_out), .sel(Operand_B[2]));
  Multiplexer #(.enable("false")) multiplexer_5 (
    .in0(multiplexer_4_out), .in1(multiplexer_39_out), .out(OUT[7]), .sel(R));
  Multiplexer #(.enable("false")) multiplexer_6 (
    .in0(Register_A[6]), .in1(Register_A[1]), .out(multiplexer_6_out), .sel(R));
  Multiplexer #(.enable("false")) multiplexer_7 (
    .in0(multiplexer_6_out), .in1(multiplexer_10_out), .out(multiplexer_7_out), .sel(Operand_B[0]));
  Multiplexer #(.enable("false")) multiplexer_8 (
    .in0(multiplexer_7_out), .in1(multiplexer_17_out), .out(multiplexer_8_out), .sel(Operand_B[1]));
  Multiplexer #(.enable("false")) multiplexer_9 (
    .in0(multiplexer_8_out), .in1(multiplexer_28_out), .out(multiplexer_9_out), .sel(Operand_B[2]));
  Multiplexer #(.enable("false")) multiplexer_10 (
    .in0(Register_A[5]), .in1(Register_A[2]), .out(multiplexer_10_out), .sel(R));
  Multiplexer #(.enable("false")) multiplexer_11 (
    .in0(multiplexer_9_out), .in1(multiplexer_34_out), .out(OUT[6]), .sel(R));
  Multiplexer #(.enable("false")) multiplexer_12 (
    .in0(multiplexer_10_out), .in1(multiplexer_16_out), .out(multiplexer_12_out), .sel(Operand_B[0]));
  Multiplexer #(.enable("false")) multiplexer_13 (
    .in0(multiplexer_12_out), .in1(multiplexer_22_out), .out(multiplexer_13_out), .sel(Operand_B[1]));
  Multiplexer #(.enable("false")) multiplexer_14 (
    .in0(multiplexer_13_out), .in1(multiplexer_33_out), .out(multiplexer_14_out), .sel(Operand_B[2]));
  Multiplexer #(.enable("false")) multiplexer_15 (
    .in0(multiplexer_14_out), .in1(multiplexer_29_out), .out(OUT[5]), .sel(R));
  Multiplexer #(.enable("false")) multiplexer_16 (
    .in0(Register_A[4]), .in1(Register_A[3]), .out(multiplexer_16_out), .sel(R));
  Multiplexer #(.enable("false")) multiplexer_17 (
    .in0(multiplexer_16_out), .in1(multiplexer_21_out), .out(multiplexer_17_out), .sel(Operand_B[0]));
  Multiplexer #(.enable("false")) multiplexer_18 (
    .in0(multiplexer_17_out), .in1(multiplexer_27_out), .out(multiplexer_18_out), .sel(Operand_B[1]));
  Multiplexer #(.enable("false")) multiplexer_19 (
    .in0(multiplexer_18_out), .in1(multiplexer_38_out), .out(multiplexer_19_out), .sel(Operand_B[2]));
  Multiplexer #(.enable("false")) multiplexer_20 (
    .in0(multiplexer_19_out), .in1(multiplexer_24_out), .out(OUT[4]), .sel(R));
  Multiplexer #(.enable("false")) multiplexer_21 (
    .in0(Register_A[3]), .in1(Register_A[4]), .out(multiplexer_21_out), .sel(R));
  Multiplexer #(.enable("false")) multiplexer_22 (
    .in0(multiplexer_21_out), .in1(multiplexer_26_out), .out(multiplexer_22_out), .sel(Operand_B[0]));
  Multiplexer #(.enable("false")) multiplexer_23 (
    .in0(multiplexer_22_out), .in1(multiplexer_32_out), .out(multiplexer_23_out), .sel(Operand_B[1]));
  Multiplexer #(.enable("false")) multiplexer_24 (
    .in0(multiplexer_23_out), .in1(Shift_In), .out(multiplexer_24_out), .sel(Operand_B[2]));
  Multiplexer #(.enable("false")) multiplexer_25 (
    .in0(multiplexer_24_out), .in1(multiplexer_19_out), .out(OUT[3]), .sel(R));
  Multiplexer #(.enable("false")) multiplexer_26 (
    .in0(Register_A[2]), .in1(Register_A[5]), .out(multiplexer_26_out), .sel(R));
  Multiplexer #(.enable("false")) multiplexer_27 (
    .in0(multiplexer_26_out), .in1(multiplexer_31_out), .out(multiplexer_27_out), .sel(Operand_B[0]));
  Multiplexer #(.enable("false")) multiplexer_28 (
    .in0(multiplexer_27_out), .in1(multiplexer_37_out), .out(multiplexer_28_out), .sel(Operand_B[1]));
  Multiplexer #(.enable("false")) multiplexer_29 (
    .in0(multiplexer_28_out), .in1(Shift_In), .out(multiplexer_29_out), .sel(Operand_B[2]));
  Multiplexer #(.enable("false")) multiplexer_30 (
    .in0(multiplexer_29_out), .in1(multiplexer_14_out), .out(OUT[2]), .sel(R));
  Multiplexer #(.enable("false")) multiplexer_31 (
    .in0(Register_A[1]), .in1(Register_A[6]), .out(multiplexer_31_out), .sel(R));
  Multiplexer #(.enable("false")) multiplexer_32 (
    .in0(multiplexer_31_out), .in1(multiplexer_36_out), .out(multiplexer_32_out), .sel(Operand_B[0]));
  Multiplexer #(.enable("false")) multiplexer_33 (
    .in0(multiplexer_32_out), .in1(Shift_In), .out(multiplexer_33_out), .sel(Operand_B[1]));
  Multiplexer #(.enable("false")) multiplexer_34 (
    .in0(multiplexer_33_out), .in1(Shift_In), .out(multiplexer_34_out), .sel(Operand_B[2]));
  Multiplexer #(.enable("false")) multiplexer_35 (
    .in0(multiplexer_34_out), .in1(multiplexer_9_out), .out(OUT[1]), .sel(R));
  Multiplexer #(.enable("false")) multiplexer_36 (
    .in0(Register_A[0]), .in1(Register_A[7]), .out(multiplexer_36_out), .sel(R));
  Multiplexer #(.enable("false")) multiplexer_37 (
    .in0(multiplexer_36_out), .in1(Shift_In), .out(multiplexer_37_out), .sel(Operand_B[0]));
  Multiplexer #(.enable("false")) multiplexer_38 (
    .in0(multiplexer_37_out), .in1(Shift_In), .out(multiplexer_38_out), .sel(Operand_B[1]));
  Multiplexer #(.enable("false")) multiplexer_39 (
    .in0(multiplexer_38_out), .in1(Shift_In), .out(multiplexer_39_out), .sel(Operand_B[2]));
  Multiplexer #(.enable("false")) multiplexer_40 (
    .in0(multiplexer_39_out), .in1(multiplexer_4_out), .out(OUT[0]), .sel(R));
endmodule

module ALU (
  input  [7:0] Register_A,
  input  [7:0] Operand_B,
  input  [7:0] RegB_Komplement,
  input  Do_B_Comp,
  output [7:0] OUT,
  output Cout,
  output Borrow
);

  wire fulladder_1_cout, fulladder_2_cout, fulladder_3_cout, fulladder_4_cout, fulladder_5_cout,
       fulladder_6_cout, fulladder_7_cout;
  wire [7:0] multiplexer_1_out;

  Multiplexer #(.width(8), .enable("false")) multiplexer_1 (
    .in0(Operand_B), .in1(RegB_Komplement), .out(multiplexer_1_out), .sel(Do_B_Comp));
  FullAdder fulladder_1 (
    .A(Register_A[0]), .B(multiplexer_1_out[0]), .Cin(1'b1), .Out(OUT[0]), .Cout(fulladder_1_cout));
  FullAdder fulladder_2 (
    .A(Register_A[1]), .B(multiplexer_1_out[1]), .Cin(fulladder_1_cout), .Out(OUT[1]), .Cout(fulladder_2_cout));
  FullAdder fulladder_3 (
    .A(Register_A[2]), .B(multiplexer_1_out[2]), .Cin(fulladder_2_cout), .Out(OUT[2]), .Cout(fulladder_3_cout));
  FullAdder fulladder_4 (
    .A(Register_A[3]), .B(multiplexer_1_out[3]), .Cin(fulladder_3_cout), .Out(OUT[3]), .Cout(fulladder_4_cout));
  FullAdder fulladder_5 (
    .A(Register_A[4]), .B(multiplexer_1_out[4]), .Cin(fulladder_4_cout), .Out(OUT[4]), .Cout(fulladder_5_cout));
  FullAdder fulladder_6 (
    .A(Register_A[5]), .B(multiplexer_1_out[5]), .Cin(fulladder_5_cout), .Out(OUT[5]), .Cout(fulladder_6_cout));
  FullAdder fulladder_7 (
    .A(Register_A[6]), .B(multiplexer_1_out[6]), .Cin(fulladder_6_cout), .Out(OUT[6]), .Cout(fulladder_7_cout));
  FullAdder fulladder_8 (
    .A(Register_A[7]), .B(multiplexer_1_out[7]), .Cin(fulladder_7_cout), .Out(OUT[7]), .Cout(Cout));
  not not_1 (Borrow, Cout);
endmodule

module Temp_Reg (
  input  [7:0] DATA_BUS_IN,
  input  LATCH_L,
  input  LATCH_H,
  input  CLK,
  input  RESET,
  input  OE_ADR,
  input  OE_DATA,
  output [7:0] DATA_BUS_OUT,
  output [13:0] ADR_BUS_OUT,
  output OE_ADR_2,
  output OE_DATA_2
);

  wire [7:6] register_2_q;

  Register register_1 (.D(DATA_BUS_IN), .en(LATCH_L), .Q(ADR_BUS_OUT[7:0]), .clk(CLK), .clr(RESET));
  Register register_2 (.D(DATA_BUS_IN), .en(LATCH_H), .Q({register_2_q, ADR_BUS_OUT[13:8]}), .clk(CLK), .clr(RESET));

  assign DATA_BUS_OUT = ADR_BUS_OUT[7:0];
  assign OE_ADR_2 = OE_ADR;
  assign OE_DATA_2 = OE_DATA;
endmodule

module Logic (
  input  [1:0] DUAL_OP_CODE,
  input  [7:0] Register_A,
  input  [7:0] Operand_B,
  input  [7:0] Register_B,
  input  KOMP,
  input  NOT,
  input  DUAL_OP_OE,
  output [7:0] Register_B_Complement,
  output [7:0] OUT,
  output OUTPUT_EN
);

  wire and_1_out, and_2_out, and_3_out, and_5_out, and_6_out, and_7_out, not_1_out, not_2_out;
  wire [7:0] and_4_out, not_3_out, or_2_out, xor_1_out;

  and and_1 (and_1_out, not_2_out, not_1_out);
  not not_1 (not_1_out, DUAL_OP_CODE[0]);
  not not_2 (not_2_out, DUAL_OP_CODE[1]);
  and and_2 (and_2_out, not_2_out, DUAL_OP_CODE[0]);
  and and_3 (and_3_out, DUAL_OP_CODE[1], not_1_out);
  or or_1 (OUTPUT_EN, KOMP, DUAL_OP_OE, NOT);
  assign not_3_out = ~Register_A;  // NOT_Gate not_3, 8 bits wide
  assign OUT = NOT ? not_3_out : 8'bz;  // Controlled_Buffer controlled_buffer_1
  Pull_Resistor pull_resistor_1 (.node(OUT));
  assign and_4_out = Register_A & Operand_B;  // AND_Gate and_4, 8 bits wide
  and and_5 (and_5_out, and_1_out, DUAL_OP_OE);
  assign OUT = and_5_out ? and_4_out : 8'bz;  // Controlled_Buffer controlled_buffer_2
  and and_6 (and_6_out, and_2_out, DUAL_OP_OE);
  assign or_2_out = Register_A | Operand_B;  // OR_Gate or_2, 8 bits wide
  assign OUT = and_6_out ? or_2_out : 8'bz;  // Controlled_Buffer controlled_buffer_3
  assign xor_1_out = Register_A ^ Operand_B;  // XOR_Gate xor_1, 8 bits wide
  and and_7 (and_7_out, and_3_out, DUAL_OP_OE);
  assign OUT = and_7_out ? xor_1_out : 8'bz;  // Controlled_Buffer controlled_buffer_4
  Complementer complementer_1 (.IN(Register_B), .OUT(Register_B_Complement));
  assign OUT = KOMP ? Register_B_Complement : 8'bz;  // Controlled_Buffer controlled_buffer_5
endmodule

module Inst_Reg (
  input  [15:0] Inst_Input,
  input  LATCH_EN,
  input  CLK,
  input  RESET,
  output [15:0] Inst_Output
);

  Register #(.width(16)) register_1 (.D(Inst_Input), .en(LATCH_EN), .Q(Inst_Output), .clk(CLK), .clr(RESET));
endmodule

module ROM (
  input  [13:0] PC_IN,
  output [15:0] INST_OUT
);

  ROM_part #(.addrWidth(14), .dataWidth(16)) rom_1 (.addr(PC_IN), .data(INST_OUT), .sel(1'b1));

  // Notes on the sheet:
  //   contents of rom_1 (hex, n*v repeats v):
  //   0 1 2 c000
endmodule

module PC (
  input  EN_LOAD,
  input  [13:0] ADR_BUS_IN,
  input  EN_CNT,
  input  CLK,
  input  RESET,
  output [13:0] PC_VAL
);

  Counter #(.width(14), .max('h3fff)) counter_1 (
    .load(EN_LOAD), .D(ADR_BUS_IN), .count(EN_CNT), .Q(PC_VAL), .clk(CLK), .clr(RESET));  // open: carry
endmodule

module main (
);

  wire CLK, RST;
  wire [1:0] inst_reg_1_inst_output_2;
  wire [7:0] control_1_ctrl_bus;
  wire [13:0] inst_reg_1_inst_output, multiplexer_1_out, pc_1_pc_val;
  wire [15:0] rom_1_inst_out;

  LED EN_LOAD (.in(control_1_ctrl_bus[3]));
  LED EN_COUNT (.in(control_1_ctrl_bus[2]));
  Multiplexer #(.width(14), .enable("false")) multiplexer_1 (
    .in0({14{1'b1}}), .in1(inst_reg_1_inst_output), .out(multiplexer_1_out), .sel(control_1_ctrl_bus[4]));
  LED EN_COUNT_2 (.in(control_1_ctrl_bus[4]));
  Button button_1 (.out(CLK));
  Button button_2 (.out(RST));
  // Probe on pc_1_pc_val
  PC pc_1 (
    .EN_LOAD(control_1_ctrl_bus[3]), .ADR_BUS_IN(multiplexer_1_out), .EN_CNT(control_1_ctrl_bus[2]),
    .CLK(CLK), .RESET(RST), .PC_VAL(pc_1_pc_val));
  ROM rom_1 (.PC_IN(pc_1_pc_val), .INST_OUT(rom_1_inst_out));
  // Probe on {inst_reg_1_inst_output_2, inst_reg_1_inst_output}
  LED EN_LOAD_2 (.in(control_1_ctrl_bus[1]));
  Inst_Reg inst_reg_1 (
    .Inst_Input(rom_1_inst_out), .LATCH_EN(control_1_ctrl_bus[1]), .CLK(CLK), .RESET(RST),
    .Inst_Output({inst_reg_1_inst_output_2, inst_reg_1_inst_output}));
  Control control_1 (
    .CLK(CLK), .RESET(RST), .CTRL_BUS(control_1_ctrl_bus),
    .INST({inst_reg_1_inst_output_2, inst_reg_1_inst_output}));

  // Notes on the sheet:
  //   PC Val:
  //   (hex)
  //   Current Inst:
  //   (hex)
endmodule

module Stack (
  input  [7:0] DATABUS_IN,
  input  EN_D_IN_LATCH,
  input  EN_DEC,
  input  EN_INC,
  input  Data_Out_Async,
  input  Data_In_Async,
  input  CLK,
  input  RESET,
  output [7:0] DATABUS_OUT
);

  wire undriven, undriven_2;
  wire [9:0] counter_1_q;

  Register register_1 (.D(DATABUS_IN), .en(EN_D_IN_LATCH), .Q(DATABUS_OUT), .clk(CLK));  // open: clr
  Counter #(.width(10), .max('h3ff)) counter_1 (
    .load(EN_DEC), .count(EN_INC), .Q(counter_1_q), .clk(CLK), .clr(RESET));  // open: D, carry
  RAM_part #(.addrWidth(10), .bus("asynch")) ram_1 (
    .addr(counter_1_q), .data(DATABUS_OUT), .sel(undriven), .ld(undriven_2), .clr(RESET));
endmodule

module RAM (
  input  [8:0] AdrBus_In,
  input  [7:0] DataBus_In,
  input  SyncLAdr,
  input  SyncLData,
  input  CLK,
  input  RESET,
  input  Async_W,
  input  Async_R,
  output [7:0] DataBus_Out
);

  wire or_1_out;
  wire [7:0] register_2_q;
  wire [8:0] register_1_q;

  Register #(.width(9)) register_1 (.D(AdrBus_In), .en(SyncLAdr), .Q(register_1_q), .clk(CLK));  // open: clr
  Register register_2 (.D(DataBus_In), .en(SyncLData), .Q(register_2_q), .clk(CLK), .clr(RESET));
  assign DataBus_Out = SyncLData ? register_2_q : 8'bz;  // Controlled_Buffer controlled_buffer_1
  or or_1 (or_1_out, Async_W, Async_R);
  RAM_part #(.addrWidth(9), .bus("asynch")) ram_1 (
    .addr(register_1_q), .data(DataBus_Out), .sel(or_1_out), .ld(Async_R), .clr(RESET));
  Pull_Resistor pull_resistor_1 (.node(DataBus_Out));
endmodule

module Control (
  input  [15:0] INST,
  input  CLK,
  input  RESET,
  output [7:0] CTRL_BUS
);

  wire not_1_out, not_2_out;
  wire [2:0] counter_1_q;
  wire [4:0] rom_1_data;

  ROM_part #(.addrWidth(7), .dataWidth(5)) rom_1 (.addr(INST[15:9]), .data(rom_1_data), .sel(1'b1));
  not not_1 (not_1_out, CTRL_BUS[0]);
  not not_2 (not_2_out, CLK);
  Counter #(.width(3), .max('h7)) counter_1 (
    .load(CTRL_BUS[0]), .D(3'b000), .count(not_1_out), .Q(counter_1_q), .clk(not_2_out), .clr(RESET));  // open: carry
  ROM_part rom_2 (.addr({rom_1_data, counter_1_q}), .data(CTRL_BUS), .sel(1'b1));

  // Notes on the sheet:
  //   Instruction Decode ROM
  //   Next_Inst
  //   contents of rom_1 (hex, n*v repeats v):
  //   0 1 2 3 4 5 6 7 8 9 a b c d e e f f 10 10 4*11 8*0 16*12 16*13 32*14 32*15
  //   MicroCode  ROM 1
  //   contents of rom_2 (hex, n*v repeats v):
  //   2 5 134*0 2 31*0 2 19
endmodule
